# Fritzing sketch BREADBOARD (saved by Fritzing 0.9.3b)
breadboards: 1
perfboards: 5

parts:
  Bauteil1 = Arduino Uno (Rev3)
  U5 = 74HC4052 [package=dil16]
  U9 = 74HC4052 [package=dil16]
  U10 = 74HC4052 [package=dil16]
  U11 = 74HC4052 [package=dil16]
  U13 = 74HC4052 [package=dil16]
  U14 = 74HC4052 [package=dil16]
  U8 = 74HC4052 [package=dil16]
  U1 = 74HC4052 [package=dil16]
  R2 = Rotary Potentiometer (Small) [maximum_resistance=100kΩ package=THT]
  R3 = Rotary Potentiometer (Small) [maximum_resistance=100kΩ package=THT]
  J1 = BANANA_CONN [package=banana_conn]  # not connected
  J2 = BANANA_CONN [package=banana_conn]  # not connected
  R4 = Slide Potentiometer [maximum_resistance=100kΩ]
  R6 = Rotary Potentiometer (Small) [maximum_resistance=100kΩ package=THT]
  J3 = BANANA_CONN [package=banana_conn]  # not connected
  J4 = BANANA_CONN [package=banana_conn]
  R7 = Rotary Potentiometer (Small) [maximum_resistance=100kΩ package=THT]
  J5 = BANANA_CONN [package=banana_conn]
  J6 = BANANA_CONN [package=banana_conn]  # not connected
  R9 = Rotary Potentiometer (Small) [maximum_resistance=100kΩ package=THT]
  R10 = Rotary Potentiometer (Small) [maximum_resistance=100kΩ package=THT]
  J7 = BANANA_CONN [package=banana_conn]  # not connected
  J8 = BANANA_CONN [package=banana_conn]  # not connected
  S4 = Toggle Switch [package=THT]  # not connected
  J9 = BANANA_CONN [package=banana_conn]
  J10 = BANANA_CONN [package=banana_conn]  # not connected
  R11 = Rotary Potentiometer (Small) [maximum_resistance=100kΩ package=THT]
  R12 = Rotary Potentiometer (Small) [maximum_resistance=100kΩ package=THT]
  J11 = BANANA_CONN [package=banana_conn]
  J12 = BANANA_CONN [package=banana_conn]
  J13 = BANANA_CONN [package=banana_conn]  # not connected
  J14 = BANANA_CONN [package=banana_conn]  # not connected
  R13 = Resistor [tolerance=±5% resistance=220 package="1206 [SMD]"]
  R14 = Resistor [tolerance=±5% resistance=220 package="1206 [SMD]"]
  R15 = Resistor [tolerance=±5% resistance=220 package="0805 [SMD]"]
  R16 = Resistor [tolerance=±5% resistance=220 package="1206 [SMD]"]
  R17 = Resistor [tolerance=±5% resistance=220 package="1206 [SMD]"]
  R18 = Resistor [tolerance=±5% resistance=220 package="0805 [SMD]"]

nets:
  N1: Bauteil1.A0, U1.Y
  N2: Bauteil1.A3, U5.X0
  N3: Bauteil1.A4/SDA, U5.X3
  N4: Bauteil1.A5/SCL, U5.A
  N5: Bauteil1.D8, U10.X3, U14.X3, U8.X3
  N6: Bauteil1.D9_PWM, U10.A, U14.A, U8.A
  N7: Bauteil1.D10_PWM/SS, U10.B, U14.B, U8.B
  N8: Bauteil1.D11_PWM/MOSI, U9.X3, U11.X3, U1.X3
  N9: Bauteil1.D12/MISO, U9.A, U11.A, U1.A
  N10: Bauteil1.D13/SCK, U9.B, U11.B, U1.B
  N11: Bauteil1.D1/TX, U9.Y
  N12: Bauteil1.D3_PWM, U13.Y
  N13: Bauteil1.D4, U11.Y
  N14: Bauteil1.D5_PWM, U13.X3
  N15: Bauteil1.D6_PWM, U13.A
  N16: Bauteil1.D7, U13.B
  N17: U5.Y, U13.X
  GND: U5.INH, U5.VEE, U5.GND, U9.INH, U9.VEE, U9.GND, U10.INH, U10.VEE, U10.GND, U11.INH, U11.VEE, U11.GND, U13.INH, U13.VEE, U13.GND, U14.INH, U14.VEE, U14.GND, U8.INH, U8.VEE, U8.GND, U1.INH, U1.VEE, U1.GND, R13.Pin_0, R14.Pin_1, R15.Pin_0, R16.Pin_0, R17.Pin_0, R18.Pin_0
  VCC: U5.VCC, U9.VCC, U10.VCC, U11.VCC, U13.VCC, U14.VCC, U8.VCC, U1.VCC
  N18: U9.X, U8.Y
  N19: U10.Y0, U10.Y2, U10.Y1, R14.Pin_0
  N20: U10.Y, U1.X
  N21: U10.Y3, R6.wiper
  N22: U10.X0, R7.wiper
  N23: U10.X, R10.wiper
  N24: U10.X1, R9.wiper
  N25: U10.X2, R12.wiper
  N26: U11.Y0, U11.Y2, U11.Y3, U11.Y1, R16.Pin_1
  N27: U11.X0, R15.Pin_1
  N28: U11.X, U14.Y
  N29: U11.X1, J11.1
  N30: U11.X2, J12.1
  N31: U14.Y0, U14.Y2, U14.Y3, U14.Y1, R17.Pin_1
  N32: U14.X0, R18.Pin_1
  N33: U14.X, J5.1
  N34: U14.X1, J9.1
  N35: U14.X2, J4.1
  N36: U1.Y0, U1.Y2, U1.Y1, R13.Pin_1
  N37: U1.Y3, R11.wiper
  N38: U1.X0, R2.wiper
  N39: U1.X1, R4.wiper
  N40: U1.X2, R3.wiper

notes:
  A
  B
  D
  C
  A1
  B1
  D1
  C1
  VCO1
  VCO2
  OUTPUTS
  INPUTS
  CV
